# Fritzing sketch Esquematico_T04 (saved by Fritzing 0.9.2b)
breadboards: 1

parts:
  RE1 = Rotary Encoder [package=THT]
  U1 = ATTINY13 [package=dip]
  U2 = ESP32-38PinWide [part_number=ESP32-38PinWide]

nets:
  N1: RE1.EncoderPinA, U1.PB1(MISO)
  N2: RE1.EncoderPinC, U1.GND, U2.GPIO11
  N3: RE1.EncoderPinB, U1.PB4(ADC2)
  N4: U1.PB0(MOSI), U2.GPIO21
  N5: U1.PB2(SCK_ADC1), U2.GPIO22
  VCC: U1.VCC, U2.VIN

custom parts:
  ESP32-38PinWide: Generic 38-Pin ESP32 with wide format (only access to one side of pins on a breadboard) based on Stephen Lilley's HiLetgo ESP-WROOM-32 ESP32 ESP-32S Development Board.
